# Fritzing sketch Circuito (saved by Fritzing 0.9.4)
breadboards: 1

parts:
  U1 = NodeMCU V1.0
  R1 = Resistor [tolerance=±5% resistance=220 package=THT]
  LED1 = LED - 5mm [color="Red (633nm)" package="5 mm [THT]"]
  J1 = Basic Servo
  R2 = Photocell (LDR) [package=THT]
  R3 = Resistor [tolerance=±5% resistance=220 package=THT]

nets:
  N1: U1.D0, R1.Pin_1
  N2: U1.D1, J1.pulse
  GND: U1.GND, LED1.cathode, J1.gnd, R2.pin_0
  VIN: U1.Vin, J1.vcc, R3.Pin_0
  N3: U1.A0, R2.pin_1, R3.Pin_1
  N4: R1.Pin_0, LED1.anode

custom parts:
  NodeMCU V1.0: ESP8266 based NodeMCU
